# Fritzing sketch lab2 (saved by Fritzing 0.9.3b)
breadboards: 1

parts:
  Part1 = Arduino Uno (Rev3)
  LED1 = LED - 5mm [color="Yellow (595nm)" package="5 mm [THT]"]
  LED2 = LED - 5mm [color="White (8000K)" package="5 mm [THT]"]
  LED3 = LED - 5mm [color="Green (555nm)" package="5 mm [THT]"]
  R1 = Resistor [tolerance=±5% resistance=220 package=THT]
  R2 = Resistor [tolerance=±5% resistance=220 package=THT]
  R3 = Resistor [tolerance=±5% resistance=220 package=THT]

nets:
  N1: Part1.GND, LED1.cathode, LED2.cathode, LED3.cathode
  N2: Part1.D5_PWM, R1.Pin_1
  N3: Part1.D6_PWM, R2.Pin_1
  N4: Part1.D7, R3.Pin_1
  N5: LED1.anode, R3.Pin_0
  N6: LED2.anode, R2.Pin_0
  N7: LED3.anode, R1.Pin_0

notes:
  Lab#2 multiple led blink
  LED Yellow : D7
  LED White : D6
  LED Green : D5
  Panya Thongkumdee
  Aug , 21 , 2017
