# Fritzing sketch lab4 (saved by Fritzing 0.9.3b)
breadboards: 1

parts:
  RHT1 = Humidity and Temperature Sensor RHT03
  Part1 = Arduino Uno (Rev3)
  LED1 = LED - 5mm [color="Red (633nm)" package="5 mm [THT]"]
  R1 = Resistor [tolerance=±5% resistance=220 package=THT]

nets:
  VCC: RHT1.Vcc, RHT1.Data-signal, Part1.D2, Part1.5V
  N1: RHT1.GND_2, Part1.GND, LED1.cathode
  N2: Part1.D13/SCK, R1.Pin_1
  N3: LED1.anode, R1.Pin_0

notes:
  D2 : Data
  D13 : LED
  Panya Thongkumdee
  Aug , 21 , 2017
